// Logisim project ALU.circ as structural Verilog
module ALU (
  input  [3:0] in_1,
  input  [2:0] select,
  input  [19:0] B,
  input  [19:0] A,
  output [19:0] Y,
  output zero
);

  wire [2:0] undriven_2;
  wire [19:0] adder_1_out, AND_out, divider_1_out, multiplier_1_out, OR_out, subtractor_1_out, undriven,
       XOR_out;

  Adder #(.width(20)) adder_1 (.a(A), .b(B), .out(adder_1_out));  // open: cin, cout
  Subtractor #(.width(20)) subtractor_1 (.a(A), .b(B), .out(subtractor_1_out));  // open: bin, bout
  Multiplier #(.width(20)) multiplier_1 (.a(A), .b(B), .out(multiplier_1_out));  // open: cin, cout
  Divider #(.width(20)) divider_1 (.a(A), .b(B), .out(divider_1_out));  // open: upper, rem
  assign AND_out = A & B;  // AND_Gate AND, 20 bits wide
  assign OR_out = A | B;  // OR_Gate OR, 20 bits wide
  assign XOR_out = A ^ B;  // XOR_Gate XOR, 20 bits wide
  Multiplexer #(.select(3), .width(20), .enable("false")) multiplexer_1 (
    .in0(undriven), .in1(adder_1_out), .in2(subtractor_1_out), .in3(multiplier_1_out), .in4(divider_1_out),
    .in5(AND_out), .in6(OR_out), .in7(XOR_out), .out(Y), .sel(undriven_2));
  nand Zero_Check (zero, Y[0], Y[1], Y[2], Y[3], Y[4], Y[5], Y[6], Y[7], Y[8], Y[9], Y[11], Y[12], Y[13], Y[14], Y[15], Y[16], Y[17], Y[18], Y[19]);
endmodule
