// Logisim project Control Unit .circ as structural Verilog: 3 circuits, main circuit main
module main (
);

  AND_with_not and_with_not_1 ();
endmodule

module Control_Unit (
  input  [3:0] opcode,
  output [2:0] out_2,
  output out_3,
  output out_4,
  output out_5,
  output out_6,
  output branch,
  output out_8,
  output out_9
);

  wire not_1_out, not_2_out, not_3_out, not_4_out, not_5_out, not_6_out, not_7_out, not_8_out, not_9_out,
       not_10_out, not_11_out, not_12_out;

  not not_1 (not_1_out, opcode[3]);
  not not_2 (not_2_out, opcode[2]);
  not not_3 (not_3_out, opcode[1]);
  not not_4 (not_4_out, opcode[0]);
  not not_5 (not_5_out, opcode[3]);
  not not_6 (not_6_out, opcode[2]);
  not not_7 (not_7_out, opcode[1]);
  not not_8 (not_8_out, opcode[3]);
  not not_9 (not_9_out, opcode[2]);
  not not_10 (not_10_out, opcode[0]);
  not not_11 (not_11_out, opcode[3]);
  not not_12 (not_12_out, opcode[2]);
  and and_1 (out_2[2], not_1_out, not_2_out, not_3_out, not_4_out);
  and and_2 (out_6, not_5_out, not_6_out, not_7_out, opcode[0]);
  and and_3 (branch, not_8_out, not_9_out, opcode[1], not_10_out);
  and and_4 (out_2[1], not_11_out, not_12_out, opcode[1], opcode[0]);
  or or_1 (out_3, out_2[2], out_6);
  or or_2 (out_5, out_6, branch);
  or or_3 (out_9, out_6, branch);
  or or_4 (out_2[0], out_6, branch);

  assign out_4 = out_2[2];
  assign out_8 = out_2[1];

  // Notes on the sheet:
  //   Aluop
  //   R-type
  //   lw
  //   sw
  //   beq
  //   RegWrite
  //   RegDst
  //   AluSrc
  //   MemToReg
  //   MemWite
  //   extOp
endmodule

module AND_with_not (
);

  wire and_1_out, undriven;

  and and_1 (and_1_out, undriven, undriven);
endmodule
