// Logisim project registerFile.circ as structural Verilog
module Register_File (
  input  [3:0] RegAdress,
  input  [19:0] writeData,
  input  controlR_W,
  input  clock,
  input  [3:0] reg2,
  input  [3:0] reg1,
  output [19:0] reg1Output,
  output [19:0] reg2Output
);

  wire and_1_out, and_2_out, and_3_out, and_4_out, and_5_out, and_6_out, and_7_out, and_8_out, and_9_out,
       and_10_out, and_11_out, and_12_out, and_13_out, and_14_out, and_15_out, and_16_out, decoder_1_out0,
       decoder_1_out1, decoder_1_out2, decoder_1_out3, decoder_1_out4, decoder_1_out5, decoder_1_out6,
       decoder_1_out7, decoder_1_out8, decoder_1_out9, decoder_1_out10, decoder_1_out11, decoder_1_out12,
       decoder_1_out13, decoder_1_out14, decoder_1_out15;
  wire [19:0] register_1_q, register_2_q, register_3_q, register_4_q, register_5_q, register_6_q,
       register_7_q, register_8_q, register_9_q, register_10_q, register_11_q, register_12_q, register_13_q,
       register_14_q, register_15_q, register_16_q;

  Decoder #(.select(4), .enable("false")) decoder_1 (
    .out0(decoder_1_out0), .out1(decoder_1_out1), .out2(decoder_1_out2), .out3(decoder_1_out3),
    .out4(decoder_1_out4), .out5(decoder_1_out5), .out6(decoder_1_out6), .out7(decoder_1_out7),
    .out8(decoder_1_out8), .out9(decoder_1_out9), .out10(decoder_1_out10), .out11(decoder_1_out11),
    .out12(decoder_1_out12), .out13(decoder_1_out13), .out14(decoder_1_out14), .out15(decoder_1_out15),
    .sel(RegAdress));
  and and_1 (and_1_out, decoder_1_out0, controlR_W);
  and and_2 (and_2_out, decoder_1_out1, controlR_W);
  and and_3 (and_3_out, decoder_1_out2, controlR_W);
  and and_4 (and_4_out, decoder_1_out3, controlR_W);
  and and_5 (and_5_out, decoder_1_out4, controlR_W);
  and and_6 (and_6_out, decoder_1_out5, controlR_W);
  and and_7 (and_7_out, decoder_1_out6, controlR_W);
  and and_8 (and_8_out, decoder_1_out7, controlR_W);
  Register #(.width(20)) register_1 (.D(writeData), .Q(register_1_q), .clk(clock), .clr(and_1_out));  // open: en
  Register #(.width(20)) register_2 (.D(writeData), .Q(register_2_q), .clk(clock), .clr(and_2_out));  // open: en
  Register #(.width(20)) register_3 (.D(writeData), .Q(register_3_q), .clk(clock), .clr(and_3_out));  // open: en
  Register #(.width(20)) register_4 (.D(writeData), .Q(register_4_q), .clk(clock), .clr(and_4_out));  // open: en
  Register #(.width(20)) register_5 (.D(writeData), .Q(register_5_q), .clk(clock), .clr(and_5_out));  // open: en
  Register #(.width(20)) register_6 (.D(writeData), .Q(register_6_q), .clk(clock), .clr(and_6_out));  // open: en
  Register #(.width(20)) register_7 (.D(writeData), .Q(register_7_q), .clk(clock), .clr(and_7_out));  // open: en
  Register #(.width(20)) register_8 (.D(writeData), .Q(register_8_q), .clk(clock), .clr(and_8_out));  // open: en
  and and_9 (and_9_out, decoder_1_out8, controlR_W);
  and and_10 (and_10_out, decoder_1_out9, controlR_W);
  and and_11 (and_11_out, decoder_1_out10, controlR_W);
  and and_12 (and_12_out, decoder_1_out11, controlR_W);
  and and_13 (and_13_out, decoder_1_out12, controlR_W);
  and and_14 (and_14_out, decoder_1_out13, controlR_W);
  and and_15 (and_15_out, decoder_1_out14, controlR_W);
  and and_16 (and_16_out, decoder_1_out15, controlR_W);
  Register #(.width(20)) register_9 (.D(writeData), .Q(register_9_q), .clk(clock), .clr(and_9_out));  // open: en
  Register #(.width(20)) register_10 (.D(writeData), .Q(register_10_q), .clk(clock), .clr(and_10_out));  // open: en
  Register #(.width(20)) register_11 (.D(writeData), .Q(register_11_q), .clk(clock), .clr(and_11_out));  // open: en
  Register #(.width(20)) register_12 (.D(writeData), .Q(register_12_q), .clk(clock), .clr(and_12_out));  // open: en
  Register #(.width(20)) register_13 (.D(writeData), .Q(register_13_q), .clk(clock), .clr(and_13_out));  // open: en
  Register #(.width(20)) register_14 (.D(writeData), .Q(register_14_q), .clk(clock), .clr(and_14_out));  // open: en
  Register #(.width(20)) register_15 (.D(writeData), .Q(register_15_q), .clk(clock), .clr(and_15_out));  // open: en
  Register #(.width(20)) register_16 (.Q(register_16_q), .clk(clock), .clr(and_16_out));  // open: D, en
  Multiplexer #(.select(4), .width(20), .enable("false")) multiplexer_1 (
    .in0(register_1_q), .in1(register_2_q), .in2(register_3_q), .in3(register_4_q), .in4(register_5_q),
    .in5(register_6_q), .in6(register_7_q), .in7(register_8_q), .in8(register_9_q), .in9(register_10_q),
    .in10(register_11_q), .in11(register_12_q), .in12(register_13_q), .in13(register_14_q),
    .in14(register_15_q), .in15(register_16_q), .out(reg1Output), .sel(reg1));
  Multiplexer #(.select(4), .width(20), .enable("false")) multiplexer_2 (
    .in0(register_1_q), .in1(register_2_q), .in2(register_3_q), .in3(register_4_q), .in4(register_5_q),
    .in5(register_6_q), .in6(register_7_q), .in7(register_8_q), .in8(register_9_q), .in9(register_10_q),
    .in10(register_11_q), .in11(register_12_q), .in12(register_13_q), .in13(register_14_q),
    .in14(register_15_q), .in15(register_16_q), .out(reg2Output), .sel(reg2));
endmodule
